# Fritzing sketch Mailbox_sensor (saved by Fritzing 0.9.3b)
circuit board: 3.21407cm x 3.71079cm

parts:
  U1 = ESP8266 WiFi Module [part_number=ESP8266]
  Q1 = NPN-Transistor [package="TO92 [THT]"]
  S1 = Reed switch [package=THT]
  R1 = Resistor [tolerance=±5% resistance=22k package=THT]
  R2 = Resistor [tolerance=±5% resistance=10k package=THT]
  LED1 = LED - 5mm [color="Red (633nm)" package="5 mm [THT]"]
  R4 = Resistor [tolerance=±5% resistance=1k package=THT]
  LED2 = LED - 5mm [color="Red (633nm)" package="5 mm [THT]"]
  R5 = Resistor [tolerance=±5% resistance=1k package=THT]
  J1 = female pin header, 2 pins [form="♀ (female)"]
  LiFePO4 = Battery
  C1 = Electrolytic Capacitor [capacitance=10µF voltage=16V package="100 mil [THT, electrolytic]"]
  R6 = Resistor [tolerance=±5% resistance=10k package=THT]

nets:
  3.3V: U1.VCC, U1.CH_PD, R1.Pin_0, R2.Pin_1, R4.Pin_0, R5.Pin_0, LiFePO4.+
  N1: U1.GPIO_0, LED2.cathode
  N2: U1.RST, Q1.C, R2.Pin_0, LED1.cathode
  GND: U1.GND, Q1.E, S1.pin_1, J1.pin2, LiFePO4.-, R6.Pin_1
  N3: Q1.B, C1.+, R6.Pin_0
  N4: S1.pin_2, R1.Pin_1, J1.pin1, C1.-
  N5: LED1.anode, R4.Pin_1
  N6: LED2.anode, R5.Pin_1

custom parts:
  ESP8266 WiFi Module: Generic WiFi Module based on the ESP8266 with onboard PCB antenna and UART communications
